# Fritzing sketch schematics (saved by Fritzing 1.0.4)
breadboards: 1

parts:
  Composant1 = Arduino Mega 2560 (Rev3)
  S1 = Pushbutton [package="[THT]"]
  S2 = Pushbutton [package="[THT]"]
  S3 = Pushbutton [package="[THT]"]
  LED1 = smd LED [color="Red (633nm)" package="1206 [SMD]"]
  LED2 = smd LED [color="Green (555nm)" package="1206 [SMD]"]
  LED3 = smd LED [color="Blue (525nm)" package="1206 [SMD]"]
  LED4 = smd LED [color="Blue (525nm)" package="1206 [SMD]"]
  LED5 = smd LED [color="Blue (525nm)" package="1206 [SMD]"]
  R1 = Resistor [tolerance=±5% resistance=100 package="0402 [SMD]"]
  SG1 = Buzzer 12mm [part_number=COM-07950 package=buzzer-12mm-ns]
  Composant2 = LED Matrix - Serial Interface - Red/Green/Blue

nets:
  GND: Composant1.GND, S1.Pin_1, S1.Pin_2, S2.Pin_1, S2.Pin_2, S3.Pin_1, S3.Pin_2, SG1.2, Composant2.GND
  N1: Composant1.D10_PWM, SG1.1
  N2: Composant1.D9_PWM, LED3.cathode
  N3: Composant1.D8_PWM, LED5.cathode
  N4: Composant1.D2_PWM, S1.Pin_3, S1.Pin_4
  N5: Composant1.D3_PWM, S2.Pin_3, S2.Pin_4
  N6: Composant1.D4_PWM, S3.Pin_3, S3.Pin_4
  N7: Composant1.D5_PWM, LED1.cathode
  N8: Composant1.D6_PWM, LED2.cathode
  N9: Composant1.D7_PWM, LED4.cathode
  5V: Composant1.5V, LED1.anode, LED2.anode, LED3.anode, LED4.anode, LED5.anode, R1.Pin_0, R1.Pin_1, Composant2.VCC
  N10: Composant1.D49, Composant2.MISO
  N11: Composant1.D51, Composant2.SCK

custom parts:
  Buzzer 12mm: Buzzer 12mm Spark Fun Electronics SKU : Comp-Buzzer Through hole This is a small 12mm round speaker that operates around the audible 2kHz range. You can use these speakers to create simple music or user interfaces. This is not a true piezoelectric speaker but behaves similarly. Instead of a piezoelectric crystal that vibrates with an electric current, this tiny speaker uses an electromagnet to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
